# Fritzing sketch Schaltplan (saved by Fritzing 0.9.3b)
breadboards: 1

parts:
  M1 = DOIT Esp32 DevKit v1 (30 pins long, 11 pins width) [part_number=ESP32S-PIN30]
  M2 = DC Motor
  M4 = DC Motor
  M5 = DC Motor
  U4 = LIPO-1000mAh [package=lipo-1000]
  S1 = H-Bridge with L298N
  S2 = H-Bridge with L298N
  M6 = DC Motor
  GY1 = MPU-6050 Board GY-521 [form="♀ (female)" package=THT]
  S3 = Toggle Switch [package=THT]
  U5 = LIPO-1000mAh [package=lipo-1000]
  Power_plug1 = Power plug
  R1 = Resistor [tolerance=±5% resistance=220 package=THT]
  R2 = Resistor [tolerance=±5% resistance=220 package=THT]  # not connected
  R3 = Resistor [tolerance=±5% resistance=220 package=THT]

nets (from the breadboard view):
  N1: M1.3V3, GY1.pin1
  GND: M1.GND, S1.GND, S2.GND, GY1.pin2, R1.Pin_0
  N2: M1.D15, S1.IN1
  N3: M1.D4, S1.ENA
  N4: M1.RX2, S2.ENA
  N5: M1.TX2, S2.IN1
  N6: M1.D5, S2.IN2
  N7: M1.D18, S2.IN3
  N8: M1.D19, S2.IN4
  N9: M1.D21, GY1.pin4
  N10: M1.RX0, S1.IN2
  N11: M1.D22, GY1.pin3
  N12: M1.D23, S2.ENB
  N13: M1.D32, S1.ENB
  N14: M1.D12, S1.IN4
  N15: M1.D13, S1.IN3
  VIN: M1.VIN, S2.5V
  N16: M2.pin_1, S2.M1-02
  N17: M2.pin_2, S2.M1-01
  N18: M4.pin_1, S1.M1-02
  N19: M4.pin_2, S1.M1-01
  N20: M5.pin_1, S2.M2-02
  N21: M5.pin_2, S2.M2-01
  N22: U4.-, U5.+
  12V: S1.12V, S2.12V, S3.L2
  N23: S1.M2-01, M6.pin_2
  N24: S1.M2-02, M6.pin_1
  N25: S3.L1, R3.Pin_1
  N26: S3.COM, Power_plug1.GND

custom parts:
  DOIT Esp32 DevKit v1 (30 pins long, 11 pins width): The DOIT Esp32 DevKit v1 is one of the development board created by DOIT to evaluate the ESP-WROOM-32 module. It is based on the ESP32 microcontroller that boasts Wifi, Bluetooth, Ethernet and Low Power support all in a single chip. (vanepp) made breadboard work, adjusted pin numbering and labels and reduced size of schematic and cleaned up pcb. This chip is 30pins long (2 x15) and 11 pins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
  H-Bridge with L298N: h-bridge
  MPU-6050 Board GY-521: Acelerometro y Giroscopio MPU-6050 Board GY-521
